# Fritzing sketch giveMeTheBinary (saved by Fritzing 0.9.3b)
breadboards: 1

parts:
  Componente1 = Arduino Uno (Rev3)
  LED1 = LED - 5mm [color="Red (633nm)" package="5 mm [THT]"]
  LED2 = LED - 5mm [color="Green (555nm)" package="5 mm [THT]"]
  LED3 = LED - 5mm [color="Green (555nm)" package="5 mm [THT]"]
  LED4 = LED - 5mm [color="Green (555nm)" package="5 mm [THT]"]
  LED5 = LED - 5mm [color="Green (555nm)" package="5 mm [THT]"]
  S3 = Momentary Switch [package=ksa_sealed_tac_switch]
  R1 = Resistor [tolerance=±5% resistance=220 package=THT]
  R2 = Resistor [tolerance=±5% resistance=10k package=THT]
  S4 = Momentary Switch [package=ksa_sealed_tac_switch]
  R3 = Resistor [tolerance=±5% resistance=220 package=THT]
  R4 = Resistor [tolerance=±5% resistance=10k package=THT]
  S5 = Momentary Switch [package=ksa_sealed_tac_switch]
  R5 = Resistor [tolerance=±5% resistance=220 package=THT]
  R6 = Resistor [tolerance=±5% resistance=10k package=THT]
  S6 = Momentary Switch [package=ksa_sealed_tac_switch]
  R7 = Resistor [tolerance=±5% resistance=220 package=THT]
  R8 = Resistor [tolerance=±5% resistance=10k package=THT]
  R9 = Resistor [tolerance=±5% resistance=220 package=THT]
  R10 = Rotary Potentiometer (Small) [maximum_resistance=100kΩ package=THT]
  U1 = LCD-16X2 [package=lcd-16x2]

nets:
  N1: Componente1.A0, R10.wiper
  N2: Componente1.A1, R9.Pin_1
  N3: Componente1.A2, R3.Pin_1
  N4: Componente1.A3, S3.4, R2.Pin_1
  N5: Componente1.D8, U1.E
  N6: Componente1.D9_PWM, S4.1, U1.DB4
  N7: Componente1.D10_PWM/SS, U1.DB5
  N8: Componente1.D11_PWM/MOSI, S4.3, U1.DB6
  N9: Componente1.D12/MISO, U1.DB7
  N10: Componente1.D13/SCK, R1.Pin_1
  N11: Componente1.D2, S4.4, R4.Pin_1
  N12: Componente1.D3_PWM, S5.4, R6.Pin_1
  N13: Componente1.D4, S6.4, R8.Pin_1
  N14: Componente1.D5_PWM, R7.Pin_1
  N15: Componente1.D6_PWM, R5.Pin_1
  N16: Componente1.D7, U1.RS
  5V: Componente1.5V, S3.2, S4.2, S5.2, S6.2, R10.leg1, U1.VDD, U1.A
  GND: Componente1.GND, LED1.cathode, LED2.cathode, LED3.cathode, LED4.cathode, LED5.cathode, R2.Pin_0, R4.Pin_0, R6.Pin_0, R8.Pin_0, R10.leg2, U1.VSS, U1.VO, U1.R_W, U1.K
  N17: LED1.anode, R9.Pin_0
  N18: LED2.anode, R1.Pin_0
  N19: LED3.anode, R7.Pin_0
  N20: LED4.anode, R5.Pin_0
  N21: LED5.anode, R3.Pin_0
